# Fritzing sketch Plank (saved by Fritzing 0.9.9b)
breadboards: 1

parts:
  J2 = Camdenboss CTB0158-2 [part_number=CTB0158-2 package=THT]
  R2 = Resistor [tolerance=±5% resistance=47 package="0603 [SMD]"]
  J3 = Camdenboss CTB0158-2 [part_number=CTB0158-2 package=THT]
  LED1 = smd LED [color="Red (633nm)" package="0603 [SMD]"]

nets:
  N1: J2.pin1, R2.Pin_0
  N2: J2.pin2, J3.pin1, LED1.cathode
  N3: R2.Pin_1, J3.pin2, LED1.anode

notes:
  GND
  3V
  COM
  Volt/Amp/Ohm
