# Fritzing sketch RLC (saved by Fritzing 0.9.9b)
breadboards: 1

parts:
  J2 = Camdenboss CTB0158-2 [part_number=CTB0158-2 package=THT]
  R2 = Resistor [tolerance=±5% resistance=47 package="0603 [SMD]"]
  C1 = Capacitor [package=cap-pth-small2]
  J1 = Camdenboss CTB0158-3 [part_number=CTB0158-3 package=THT]
  L2 = Inductors [package=cdrh2d09]

nets:
  N1: J2.pin1, C1.1, J1.pin3
  N2: J2.pin2, R2.Pin_0, J1.pin1
  N3: R2.Pin_1, L2.2
  N4: C1.2, J1.pin2, L2.1

notes:
  Signal from Generator
  Ground
  OScope Channel 1
  Oscope Channel 2
  Ground
