# Fritzing sketch bandpassAmp (saved by Fritzing 0.9.9b)
breadboards: 1

parts:
  Cf_-_1nF = Capacitor [package=cap-pth-small2]
  Cin_-_100nF = Capacitor [package=cap-pth-small2]
  Rf = Resistor [tolerance=±5% resistance=10k package="0805 [SMD]"]
  Rin = Resistor [tolerance=±5% power=0.25 resistance=1k package=THT]
  J1 = Camdenboss CTB0158-3 [part_number=CTB0158-3 package=THT]
  U1 = OP27 - Low Noise, Precision Op Amp [part_number=OP27]
  J2 = Camdenboss CTB0158-2 [package=THT]

nets:
  N1: Cf_-_1nF.1, Cin_-_100nF.2, Rf.Pin_0, U1.-IN
  N2: Cf_-_1nF.2, Rf.Pin_1, U1.OUT
  N3: Cin_-_100nF.1, Rin.Pin_1
  N4: Rin.Pin_0, J2.pin1
  N5: J1.pin1, U1.V+
  N6: J1.pin2, U1.+IN, J2.pin2
  N7: J1.pin3, U1.-V

notes:
  Sig GND
  +12 GND -12
