# Fritzing sketch ugly741 (saved by Fritzing 0.9.9b)
breadboards: 1

parts:
  LM1 = LM741 [part_number=LM741 package="DIP (Dual Inline) [THT]"]
  R1 = Resistor [tolerance=±5% power=0.25 resistance=220 package=THT]
  C2 = Capacitor [package=cap-pth-small2]
  R2 = Resistor [tolerance=±5% power=0.25 resistance=220 package=THT]
  C1 = Capacitor [package=cap-pth-small2]

nets:
  N1: LM1.pin2, R2.Pin_1
  N2: LM1.pin6, R1.Pin_1, C1.2
  N3: R1.Pin_0, C1.1
  N4: C2.2, R2.Pin_0

notes:
  10k resistor
  68 nF capacitor
  1k resistor
  1 nF capacitor

custom parts:
  LM741: This is a single Op Amp DIP.
